// Logisim project r_a_m_Engine.circ as structural Verilog: 1 circuit, main circuit main
module main (
  input  FEEDBACK,
  input  STORE,
  input  SELECTOR,
  input  OUTPUT,
  input  _1,
  input  MODE,
  input  RESET,
  input  _2,
  input  _4,
  input  _8
);

  wire adder_1_cout, adder_1_out, adder_2_cout, adder_2_out, adder_3_cout, adder_3_out, adder_4_cout,
       adder_4_out, and_1_out, and_2_out, and_3_out, and_4_out, and_5_out, and_6_out, d_ff_1_q, d_ff_2_q,
       d_ff_3_q, d_ff_4_q, d_ff_5_q, d_ff_6_q, d_ff_7_q, d_ff_8_q, d_ff_9_q, d_ff_9_qn, d_ff_10_q,
       d_ff_10_qn, d_ff_11_q, d_ff_11_qn, d_ff_12_q, d_ff_12_qn, d_ff_13_q, demultiplexer_1_out0,
       demultiplexer_1_out1, demultiplexer_2_out0, demultiplexer_2_out1, demultiplexer_3_out0,
       demultiplexer_3_out1, demultiplexer_4_out0, demultiplexer_4_out1, not_1_out, not_2_out, not_3_out,
       not_4_out, not_5_out, or_1_out, or_2_out, or_3_out, or_4_out, or_5_out, xor_1_out, xor_2_out,
       xor_3_out, xor_4_out;

  or or_1 (or_1_out, FEEDBACK, STORE);
  Demultiplexer demultiplexer_1 (.out0(demultiplexer_1_out0), .out1(demultiplexer_1_out1), .in(_1), .sel(SELECTOR));
  Demultiplexer demultiplexer_2 (.out0(demultiplexer_2_out0), .out1(demultiplexer_2_out1), .in(_2), .sel(SELECTOR));
  Demultiplexer demultiplexer_3 (.out0(demultiplexer_3_out0), .out1(demultiplexer_3_out1), .in(_4), .sel(SELECTOR));
  Demultiplexer demultiplexer_4 (.out0(demultiplexer_4_out0), .out1(demultiplexer_4_out1), .in(_8), .sel(SELECTOR));
  not not_1 (not_1_out, SELECTOR);
  and and_1 (and_1_out, not_1_out, or_1_out);
  and and_2 (and_2_out, SELECTOR, or_1_out);
  or or_2 (or_2_out, and_3_out, demultiplexer_1_out0);
  or or_3 (or_3_out, and_4_out, demultiplexer_2_out0);
  or or_4 (or_4_out, and_5_out, demultiplexer_3_out0);
  or or_5 (or_5_out, and_6_out, demultiplexer_4_out0);
  D_Flip_Flop d_ff_1 (.D(or_2_out), .clk(and_1_out), .Q(d_ff_1_q), .reset(RESET));  // open: Qn, preset
  D_Flip_Flop d_ff_2 (.D(or_3_out), .clk(and_1_out), .Q(d_ff_2_q), .reset(RESET));  // open: Qn, preset
  D_Flip_Flop d_ff_3 (.D(or_4_out), .clk(and_1_out), .Q(d_ff_3_q), .reset(RESET));  // open: Qn, preset
  D_Flip_Flop d_ff_4 (.D(or_5_out), .clk(and_1_out), .Q(d_ff_4_q), .reset(RESET));  // open: Qn, preset
  D_Flip_Flop d_ff_5 (.D(demultiplexer_1_out1), .clk(and_2_out), .Q(d_ff_5_q), .reset(RESET));  // open: Qn, preset
  D_Flip_Flop d_ff_6 (.D(demultiplexer_2_out1), .clk(and_2_out), .Q(d_ff_6_q), .reset(RESET));  // open: Qn, preset
  D_Flip_Flop d_ff_7 (.D(demultiplexer_3_out1), .clk(and_2_out), .Q(d_ff_7_q), .reset(RESET));  // open: Qn, preset
  D_Flip_Flop d_ff_8 (.D(demultiplexer_4_out1), .clk(and_2_out), .Q(d_ff_8_q), .reset(RESET));  // open: Qn, preset
  xor xor_1 (xor_1_out, d_ff_5_q, MODE);
  xor xor_2 (xor_2_out, d_ff_6_q, MODE);
  xor xor_3 (xor_3_out, d_ff_7_q, MODE);
  xor xor_4 (xor_4_out, d_ff_8_q, MODE);
  Adder #(.width(1)) adder_1 (.a(d_ff_1_q), .b(xor_1_out), .out(adder_1_out), .cin(MODE), .cout(adder_1_cout));
  Adder #(.width(1)) adder_2 (.a(d_ff_2_q), .b(xor_2_out), .out(adder_2_out), .cin(adder_1_cout), .cout(adder_2_cout));
  Adder #(.width(1)) adder_3 (.a(d_ff_3_q), .b(xor_3_out), .out(adder_3_out), .cin(adder_2_cout), .cout(adder_3_cout));
  Adder #(.width(1)) adder_4 (.a(d_ff_4_q), .b(xor_4_out), .out(adder_4_out), .cin(adder_3_cout), .cout(adder_4_cout));
  D_Flip_Flop d_ff_9 (.D(adder_4_out), .clk(OUTPUT), .Q(d_ff_9_q), .Qn(d_ff_9_qn), .reset(RESET));  // open: preset
  D_Flip_Flop d_ff_10 (.D(adder_3_out), .clk(OUTPUT), .Q(d_ff_10_q), .Qn(d_ff_10_qn), .reset(RESET));  // open: preset
  D_Flip_Flop d_ff_11 (.D(adder_2_out), .clk(OUTPUT), .Q(d_ff_11_q), .Qn(d_ff_11_qn), .reset(RESET));  // open: preset
  D_Flip_Flop d_ff_12 (.D(adder_1_out), .clk(OUTPUT), .Q(d_ff_12_q), .Qn(d_ff_12_qn), .reset(RESET));  // open: preset
  D_Flip_Flop d_ff_13 (.D(adder_4_cout), .clk(OUTPUT), .Q(d_ff_13_q), .reset(RESET));  // open: Qn, preset
  and and_3 (and_3_out, not_2_out, FEEDBACK);
  not not_2 (not_2_out, d_ff_12_qn);
  and and_4 (and_4_out, not_3_out, FEEDBACK);
  not not_3 (not_3_out, d_ff_11_qn);
  and and_5 (and_5_out, not_5_out, FEEDBACK);
  not not_4 (not_4_out, d_ff_9_qn);
  not not_5 (not_5_out, d_ff_10_qn);
  and and_6 (and_6_out, not_4_out, FEEDBACK);
  LED led_1 (.in(d_ff_9_q));
  LED led_2 (.in(d_ff_10_q));
  LED led_3 (.in(d_ff_11_q));
  LED led_4 (.in(d_ff_12_q));
  LED led_5 (.in(d_ff_13_q));

  // Notes on the sheet:
  //   B
  //   MODE
  //   A
  //   0=ADDITION
  //   1=SUBTRACTION
  //   1
  //   2
  //   4
  //   DATA BITS
  //   SELECTOR=0
  //   8
  //   SELECTOR=1
  //   REPEATED ARITHMETIC MACHINE
  //    CORE ENGINE
  //   OUTPUT
  //   FEEDBACK
  //   SYSTEM
  //   8
  //   4
  //   2
  //   1
  //   16
endmodule
