// Logisim project r_a_mv3.circ as structural Verilog: 1 circuit, main circuit main
module main (
  input  FEEDBACK,
  input  STORE,
  input  SELECTOR,
  input  _1,
  input  MODE,
  input  RESET,
  input  _2,
  input  MULTIPLY,
  input  DIVISION,
  input  OVERRIDE,
  input  _4,
  input  _8,
  input  _1_2,
  input  _2_2,
  input  _4_2,
  input  _8_2
);

  wire adder_1_cout, adder_1_out, adder_2_cout, adder_2_out, adder_3_cout, adder_3_out, adder_4_cout,
       adder_4_out, adder_5_out, adder_6_cout, adder_6_out, adder_7_cout, adder_7_out, adder_8_cout,
       adder_8_out, and_1_out, and_2_out, and_3_out, and_4_out, and_5_out, and_6_out, and_7_out, and_8_out,
       and_9_out, and_10_out, and_11_out, and_12_out, and_13_out, and_14_out, and_15_out, and_16_out,
       and_17_out, and_18_out, and_19_out, and_20_out, and_21_out, and_22_out, and_23_out, and_24_out,
       and_25_out, and_26_out, and_27_out, and_28_out, and_29_out, and_30_out, and_31_out, and_32_out,
       and_33_out, and_34_out, and_35_out, and_36_out, and_37_out, and_38_out, and_39_out, and_40_out,
       and_41_out, and_42_out, and_43_out, and_44_out, and_45_out, and_46_out, and_47_out, and_48_out,
       and_49_out, and_50_out, and_51_out, and_52_out, and_53_out, and_54_out, and_55_out, and_56_out,
       and_57_out, and_58_out, and_59_out, and_60_out, and_61_out, and_62_out, and_63_out, and_64_out,
       and_65_out, and_66_out, and_67_out, and_68_out, and_69_out, and_70_out, and_71_out, and_72_out,
       and_73_out, and_74_out, and_75_out, and_76_out, and_77_out, and_78_out, and_79_out, and_80_out,
       and_81_out, and_82_out, and_83_out, and_84_out, and_85_out, and_86_out, and_87_out, and_88_out,
       and_89_out, and_90_out, and_91_out, and_92_out, and_93_out, and_94_out, and_95_out, and_96_out,
       and_97_out, and_98_out, and_99_out, and_100_out, and_101_out, and_102_out, and_103_out, and_104_out,
       and_105_out, and_106_out, and_107_out, and_108_out, and_109_out, and_110_out, and_111_out,
       and_112_out, and_113_out, and_114_out, and_115_out, and_116_out, and_117_out, and_118_out,
       and_119_out, and_120_out, and_121_out, and_122_out, and_123_out, and_124_out, and_125_out,
       and_126_out, and_127_out, and_128_out, and_129_out, and_130_out, and_131_out, and_132_out,
       and_133_out, and_134_out, and_135_out, and_136_out, and_137_out, and_138_out, and_139_out,
       and_140_out, and_141_out, and_142_out, and_143_out, clock_1_out, clock_2_out, d_ff_1_q, d_ff_2_q,
       d_ff_3_q, d_ff_4_q, d_ff_5_q, d_ff_6_q, d_ff_7_q, d_ff_8_q, d_ff_9_q, d_ff_10_q, d_ff_11_q, d_ff_12_q,
       d_ff_13_q, d_ff_14_q, d_ff_15_q, d_ff_16_q, d_ff_16_qn, d_ff_17_q, d_ff_17_qn, d_ff_18_q, d_ff_18_qn,
       d_ff_19_q, d_ff_19_qn, d_ff_20_q, d_ff_21_q, d_ff_22_q, d_ff_23_q, d_ff_24_q, d_ff_25_q, d_ff_26_q,
       d_ff_27_q, d_ff_28_q, d_ff_29_q, d_ff_30_q, d_ff_31_q, d_ff_32_q, d_ff_33_q, d_ff_34_q, d_ff_35_q,
       d_ff_36_q, d_ff_36_qn, d_ff_37_q, d_ff_38_q, d_ff_39_q, d_ff_40_q, d_ff_40_qn, d_ff_41_q, d_ff_42_q,
       d_ff_43_q, d_ff_43_qn, d_ff_44_q, d_ff_44_qn, d_ff_45_q, d_ff_46_q, d_ff_47_q, d_ff_47_qn, d_ff_48_q,
       d_ff_48_qn, d_ff_49_q, d_ff_50_q, d_ff_51_q, d_ff_52_q, d_ff_53_q, demultiplexer_1_out0,
       demultiplexer_1_out1, demultiplexer_2_out0, demultiplexer_2_out1, demultiplexer_3_out0,
       demultiplexer_3_out1, demultiplexer_4_out0, demultiplexer_4_out1, demultiplexer_5_out0,
       demultiplexer_5_out1, demultiplexer_6_out0, demultiplexer_6_out1, demultiplexer_7_out0,
       demultiplexer_7_out1, demultiplexer_8_out0, demultiplexer_8_out1, demultiplexer_9_out0,
       demultiplexer_9_out1, demultiplexer_10_out0, demultiplexer_10_out1, demultiplexer_11_out0,
       demultiplexer_11_out1, demultiplexer_12_out0, demultiplexer_12_out1, demultiplexer_13_out0,
       demultiplexer_13_out1, not_1_out, not_2_out, not_3_out, not_4_out, not_5_out, not_6_out, not_7_out,
       not_8_out, not_9_out, not_10_out, not_11_out, not_12_out, not_13_out, not_14_out, not_15_out,
       not_16_out, not_17_out, not_18_out, not_19_out, not_20_out, not_21_out, not_22_out, not_23_out,
       not_24_out, not_25_out, not_26_out, not_27_out, not_28_out, not_29_out, not_30_out, not_31_out,
       not_32_out, not_33_out, not_34_out, not_35_out, not_36_out, not_37_out, not_38_out, not_39_out,
       not_40_out, not_41_out, not_42_out, not_43_out, not_44_out, not_45_out, not_46_out, not_47_out,
       not_48_out, not_49_out, not_50_out, not_51_out, not_52_out, not_53_out, not_54_out, not_55_out,
       not_56_out, not_57_out, not_58_out, not_59_out, not_60_out, not_61_out, not_62_out, not_63_out,
       not_64_out, not_65_out, not_66_out, not_67_out, not_68_out, not_69_out, not_70_out, not_71_out,
       not_72_out, not_73_out, not_74_out, or_1_out, or_2_out, or_3_out, or_4_out, or_5_out, or_6_out,
       or_7_out, or_8_out, or_9_out, or_10_out, or_11_out, or_12_out, or_13_out, or_14_out, or_15_out,
       or_16_out, or_17_out, or_18_out, or_19_out, or_20_out, or_21_out, or_22_out, or_23_out, or_24_out,
       or_25_out, or_26_out, or_27_out, or_28_out, or_29_out, or_30_out, or_31_out, or_32_out, or_33_out,
       or_34_out, or_35_out, xnor_1_out, xnor_2_out, xnor_3_out, xnor_4_out, xor_1_out, xor_2_out, xor_3_out,
       xor_4_out, xor_5_out, xor_6_out, xor_7_out, xor_8_out, xor_9_out, xor_10_out, xor_11_out, xor_12_out,
       xor_13_out, xor_14_out, xor_15_out, xor_16_out;

  Clock clock_1 (.out(clock_1_out));
  or or_1 (or_1_out, and_94_out, and_15_out);
  or or_2 (or_2_out, FEEDBACK, or_1_out);
  not not_1 (not_1_out, clock_1_out);
  and and_1 (and_1_out, not_1_out, or_2_out);
  Clock clock_2 (.out(clock_2_out));
  and and_2 (and_2_out, clock_2_out, not_2_out);
  or or_3 (or_3_out, MODE, DIVISION);
  D_Flip_Flop d_ff_1 (.D(or_6_out), .clk(or_6_out), .Q(d_ff_1_q), .reset(or_5_out));  // open: Qn, preset
  not not_2 (not_2_out, d_ff_1_q);
  or or_4 (or_4_out, and_1_out, STORE);
  or or_5 (or_5_out, RESET, OVERRIDE);
  Demultiplexer demultiplexer_1 (.out0(demultiplexer_1_out0), .out1(demultiplexer_1_out1), .in(_1), .sel(SELECTOR));
  Demultiplexer demultiplexer_2 (.out0(demultiplexer_2_out0), .out1(demultiplexer_2_out1), .in(_2), .sel(SELECTOR));
  Demultiplexer demultiplexer_3 (.out0(demultiplexer_3_out0), .out1(demultiplexer_3_out1), .in(_4), .sel(SELECTOR));
  Demultiplexer demultiplexer_4 (.out0(demultiplexer_4_out0), .out1(demultiplexer_4_out1), .in(_8), .sel(SELECTOR));
  not not_3 (not_3_out, d_ff_9_q);
  not not_4 (not_4_out, d_ff_8_q);
  not not_5 (not_5_out, d_ff_7_q);
  not not_6 (not_6_out, d_ff_3_q);
  not not_7 (not_7_out, d_ff_2_q);
  not not_8 (not_8_out, d_ff_4_q);
  and and_3 (and_3_out, d_ff_7_q, d_ff_6_q);
  or or_6 (or_6_out, d_ff_49_q, and_141_out);
  not not_9 (not_9_out, SELECTOR);
  and and_4 (and_4_out, not_9_out, or_4_out);
  and and_5 (and_5_out, SELECTOR, or_4_out);
  and and_6 (and_6_out, not_3_out, not_4_out, not_5_out, d_ff_6_q);
  and and_7 (and_7_out, not_6_out, not_7_out, not_8_out, d_ff_5_q);
  or or_7 (or_7_out, d_ff_9_q, d_ff_8_q, d_ff_7_q, d_ff_6_q);
  or or_8 (or_8_out, d_ff_9_q, d_ff_8_q, d_ff_7_q);
  or or_9 (or_9_out, and_3_out, d_ff_9_q, d_ff_8_q);
  or or_10 (or_10_out, d_ff_9_q, d_ff_8_q);
  and and_8 (and_8_out, d_ff_8_q, d_ff_7_q);
  and and_9 (and_9_out, d_ff_8_q, d_ff_6_q);
  and and_10 (and_10_out, d_ff_8_q, d_ff_7_q, d_ff_6_q);
  and and_11 (and_11_out, d_ff_9_q, d_ff_8_q);
  and and_12 (and_12_out, d_ff_9_q, d_ff_7_q);
  and and_13 (and_13_out, d_ff_9_q, d_ff_6_q);
  and and_14 (and_14_out, d_ff_9_q, d_ff_8_q, d_ff_7_q, d_ff_6_q);
  not not_10 (not_10_out, d_ff_9_q);
  not not_11 (not_11_out, d_ff_8_q);
  not not_12 (not_12_out, d_ff_7_q);
  not not_13 (not_13_out, d_ff_6_q);
  or or_11 (or_11_out, and_51_out, demultiplexer_1_out0);
  or or_12 (or_12_out, and_52_out, demultiplexer_2_out0);
  or or_13 (or_13_out, and_53_out, demultiplexer_3_out0);
  or or_14 (or_14_out, and_55_out, demultiplexer_4_out0);
  and and_15 (and_15_out, MULTIPLY, or_20_out);
  or or_15 (or_15_out, d_ff_9_q, and_8_out);
  or or_16 (or_16_out, and_8_out, and_9_out, d_ff_9_q);
  or or_17 (or_17_out, and_11_out, and_12_out, and_13_out);
  and and_16 (and_16_out, not_10_out, not_11_out, not_12_out, not_13_out);
  D_Flip_Flop d_ff_2 (.D(or_11_out), .clk(and_4_out), .Q(d_ff_2_q), .reset(RESET));  // open: Qn, preset
  D_Flip_Flop d_ff_3 (.D(or_12_out), .clk(and_4_out), .Q(d_ff_3_q), .reset(RESET));  // open: Qn, preset
  D_Flip_Flop d_ff_4 (.D(or_13_out), .clk(and_4_out), .Q(d_ff_4_q), .reset(RESET));  // open: Qn, preset
  D_Flip_Flop d_ff_5 (.D(or_14_out), .clk(and_4_out), .Q(d_ff_5_q), .reset(RESET));  // open: Qn, preset
  D_Flip_Flop d_ff_6 (.D(demultiplexer_1_out1), .clk(and_5_out), .Q(d_ff_6_q), .reset(RESET));  // open: Qn, preset
  D_Flip_Flop d_ff_7 (.D(demultiplexer_2_out1), .clk(and_5_out), .Q(d_ff_7_q), .reset(RESET));  // open: Qn, preset
  D_Flip_Flop d_ff_8 (.D(demultiplexer_3_out1), .clk(and_5_out), .Q(d_ff_8_q), .reset(RESET));  // open: Qn, preset
  D_Flip_Flop d_ff_9 (.D(demultiplexer_4_out1), .clk(and_5_out), .Q(d_ff_9_q), .reset(RESET));  // open: Qn, preset
  or or_18 (or_18_out, d_ff_9_q, and_10_out);
  or or_19 (or_19_out, and_11_out, and_12_out);
  and and_17 (and_17_out, d_ff_5_q, xor_1_out);
  xor xor_1 (xor_1_out, d_ff_5_q, d_ff_9_q);
  and and_18 (and_18_out, d_ff_4_q, xor_2_out);
  xor xor_2 (xor_2_out, d_ff_4_q, d_ff_8_q);
  and and_19 (and_19_out, d_ff_9_q, xor_3_out);
  xor xor_3 (xor_3_out, d_ff_9_q, d_ff_5_q);
  and and_20 (and_20_out, d_ff_8_q, xor_4_out);
  xor xor_4 (xor_4_out, d_ff_8_q, d_ff_4_q);
  and and_21 (and_21_out, and_6_out, and_7_out);
  and and_22 (and_22_out, and_11_out, d_ff_7_q);
  and and_23 (and_23_out, d_ff_6_q, and_11_out);
  not not_14 (not_14_out, and_17_out);
  not not_15 (not_15_out, and_18_out);
  and and_24 (and_24_out, not_15_out, and_20_out);
  xor xor_5 (xor_5_out, d_ff_6_q, or_3_out);
  xor xor_6 (xor_6_out, d_ff_7_q, or_3_out);
  xor xor_7 (xor_7_out, d_ff_8_q, or_3_out);
  xor xor_8 (xor_8_out, d_ff_9_q, or_3_out);
  or or_20 (or_20_out, and_54_out, or_21_out);
  or or_21 (or_21_out, and_40_out, or_23_out);
  or or_22 (or_22_out, and_22_out, and_23_out);
  and and_25 (and_25_out, not_14_out, and_19_out);
  and and_26 (and_26_out, not_14_out, and_24_out);
  or or_23 (or_23_out, and_32_out, and_27_out);
  xor xor_9 (xor_9_out, d_ff_3_q, d_ff_7_q);
  xor xor_10 (xor_10_out, d_ff_2_q, d_ff_6_q);
  xor xor_11 (xor_11_out, d_ff_7_q, d_ff_3_q);
  xor xor_12 (xor_12_out, d_ff_6_q, d_ff_2_q);
  Adder #(.width(1)) adder_1 (.a(d_ff_2_q), .b(xor_5_out), .out(adder_1_out), .cin(or_3_out), .cout(adder_1_cout));
  and and_27 (and_27_out, and_2_out, and_33_out);
  not not_16 (not_16_out, d_ff_10_q);
  D_Flip_Flop d_ff_10 (.D(MULTIPLY), .clk(or_20_out), .Q(d_ff_10_q), .reset(RESET));  // open: Qn, preset
  D_Flip_Flop d_ff_11 (.D(and_21_out), .clk(and_21_out), .Q(d_ff_11_q), .reset(RESET));  // open: Qn, preset
  and and_28 (and_28_out, d_ff_3_q, xor_9_out);
  and and_29 (and_29_out, d_ff_2_q, xor_10_out);
  not not_17 (not_17_out, and_29_out);
  and and_30 (and_30_out, d_ff_7_q, xor_11_out);
  and and_31 (and_31_out, d_ff_6_q, xor_12_out);
  and and_32 (and_32_out, and_2_out, and_36_out);
  and and_33 (and_33_out, not_16_out, _1_2);
  and and_34 (and_34_out, _1_2, d_ff_10_q);
  D_Flip_Flop d_ff_12 (.D(d_ff_10_q), .clk(or_20_out), .Q(d_ff_12_q), .reset(RESET));  // open: Qn, preset
  not not_18 (not_18_out, and_28_out);
  and and_35 (and_35_out, not_18_out, and_30_out);
  or or_24 (or_24_out, and_25_out, and_26_out);
  Adder #(.width(1)) adder_2 (.a(d_ff_3_q), .b(xor_6_out), .out(adder_2_out), .cin(adder_1_cout), .cout(adder_2_cout));
  and and_36 (and_36_out, not_19_out, _2_2);
  not not_19 (not_19_out, d_ff_12_q);
  and and_37 (and_37_out, _2_2, d_ff_12_q);
  D_Flip_Flop d_ff_13 (.D(d_ff_12_q), .clk(or_20_out), .Q(d_ff_13_q), .reset(RESET));  // open: Qn, preset
  and and_38 (and_38_out, and_35_out, not_14_out);
  and and_39 (and_39_out, and_38_out, not_15_out);
  or or_25 (or_25_out, and_49_out, or_26_out);
  or or_26 (or_26_out, and_39_out, or_24_out);
  Adder #(.width(1)) adder_3 (.a(d_ff_4_q), .b(xor_7_out), .out(adder_3_out), .cin(adder_2_cout), .cout(adder_3_cout));
  and and_40 (and_40_out, and_2_out, and_43_out);
  not not_20 (not_20_out, d_ff_14_q);
  D_Flip_Flop d_ff_14 (.D(d_ff_13_q), .clk(or_20_out), .Q(d_ff_14_q), .reset(RESET));  // open: Qn, preset
  and and_41 (and_41_out, not_17_out, and_31_out);
  and and_42 (and_42_out, or_25_out, or_3_out);
  Adder #(.width(1)) adder_4 (.a(d_ff_5_q), .b(xor_8_out), .out(adder_4_out), .cin(adder_3_cout), .cout(adder_4_cout));
  and and_43 (and_43_out, not_20_out, _4_2);
  D_Flip_Flop d_ff_15 (.D(d_ff_14_q), .clk(or_20_out), .Q(d_ff_15_q), .reset(RESET));  // open: Qn, preset
  and and_44 (and_44_out, and_41_out, not_14_out);
  and and_45 (and_45_out, and_44_out, not_15_out);
  not not_21 (not_21_out, d_ff_22_q);
  and and_46 (and_46_out, not_21_out, and_42_out);
  D_Flip_Flop d_ff_16 (
    .D(adder_4_out), .clk(and_2_out), .Q(d_ff_16_q), .Qn(d_ff_16_qn), .reset(or_27_out));  // open: preset
  D_Flip_Flop d_ff_17 (
    .D(adder_3_out), .clk(and_2_out), .Q(d_ff_17_q), .Qn(d_ff_17_qn), .reset(or_27_out));  // open: preset
  D_Flip_Flop d_ff_18 (
    .D(adder_2_out), .clk(and_2_out), .Q(d_ff_18_q), .Qn(d_ff_18_qn), .reset(or_27_out));  // open: preset
  D_Flip_Flop d_ff_19 (
    .D(adder_1_out), .clk(and_2_out), .Q(d_ff_19_q), .Qn(d_ff_19_qn), .reset(or_27_out));  // open: preset
  D_Flip_Flop d_ff_20 (.D(adder_4_cout), .clk(and_2_out), .Q(d_ff_20_q), .reset(or_27_out));  // open: Qn, preset
  or or_27 (or_27_out, RESET, and_47_out);
  and and_47 (and_47_out, MULTIPLY, not_22_out, not_23_out, not_26_out, not_27_out);
  not not_22 (not_22_out, _4_2);
  not not_23 (not_23_out, _2_2);
  and and_48 (and_48_out, _4_2, d_ff_14_q);
  D_Flip_Flop d_ff_21 (.D(d_ff_15_q), .clk(or_20_out), .Q(d_ff_21_q), .reset(RESET));  // open: Qn, preset
  and and_49 (and_49_out, and_45_out, not_18_out);
  D_Flip_Flop d_ff_22 (.D(and_46_out), .clk(and_50_out), .Q(d_ff_22_q), .reset(or_27_out));  // open: Qn, preset
  and and_50 (and_50_out, and_46_out, not_21_out);
  and and_51 (and_51_out, not_24_out, and_1_out);
  not not_24 (not_24_out, d_ff_19_qn);
  and and_52 (and_52_out, not_25_out, and_1_out);
  not not_25 (not_25_out, d_ff_18_qn);
  not not_26 (not_26_out, _1_2);
  not not_27 (not_27_out, _8_2);
  D_Flip_Flop d_ff_23 (.D(d_ff_21_q), .clk(or_20_out), .Q(d_ff_23_q), .reset(RESET));  // open: Qn, preset
  LED led_1 (.in(and_57_out));
  LED led_2 (.in(d_ff_22_q));
  and and_53 (and_53_out, not_29_out, and_1_out);
  not not_28 (not_28_out, d_ff_16_qn);
  not not_29 (not_29_out, d_ff_17_qn);
  and and_54 (and_54_out, and_2_out, and_56_out);
  not not_30 (not_30_out, d_ff_24_q);
  D_Flip_Flop d_ff_24 (.D(d_ff_23_q), .clk(or_20_out), .Q(d_ff_24_q), .reset(RESET));  // open: Qn, preset
  and and_55 (and_55_out, not_28_out, and_1_out);
  and and_56 (and_56_out, not_30_out, _8_2);
  LED led_3 (.in(and_47_out));
  and and_57 (and_57_out, and_75_out, MULTIPLY);
  Demultiplexer demultiplexer_5 (
    .out0(demultiplexer_5_out0), .out1(demultiplexer_5_out1), .in(d_ff_16_q), .sel(and_74_out));
  Demultiplexer demultiplexer_6 (
    .out0(demultiplexer_6_out0), .out1(demultiplexer_6_out1), .in(d_ff_17_q), .sel(and_74_out));
  Demultiplexer demultiplexer_7 (
    .out0(demultiplexer_7_out0), .out1(demultiplexer_7_out1), .in(d_ff_18_q), .sel(and_74_out));
  Demultiplexer demultiplexer_8 (
    .out0(demultiplexer_8_out0), .out1(demultiplexer_8_out1), .in(d_ff_19_q), .sel(and_74_out));
  not not_31 (not_31_out, d_ff_20_q);
  and and_58 (and_58_out, _8_2, d_ff_24_q);
  not not_32 (not_32_out, d_ff_5_q);
  not not_33 (not_33_out, d_ff_4_q);
  and and_59 (and_59_out, not_32_out, not_33_out, not_34_out, not_35_out);
  not not_34 (not_34_out, d_ff_3_q);
  not not_35 (not_35_out, d_ff_2_q);
  xnor xnor_1 (xnor_1_out, d_ff_5_q, d_ff_9_q);
  xnor xnor_2 (xnor_2_out, d_ff_4_q, d_ff_8_q);
  xnor xnor_3 (xnor_3_out, d_ff_3_q, d_ff_7_q);
  xnor xnor_4 (xnor_4_out, d_ff_2_q, d_ff_6_q);
  LED led_4 (.in(demultiplexer_5_out0));
  LED led_5 (.in(demultiplexer_6_out0));
  LED led_6 (.in(demultiplexer_7_out0));
  LED led_7 (.in(demultiplexer_8_out0));
  LED led_8 (.in(d_ff_20_q));
  and and_60 (and_60_out, not_31_out, or_3_out);
  or or_28 (or_28_out, and_60_out, and_61_out);
  and and_61 (and_61_out, d_ff_20_q, or_3_out);
  and and_62 (and_62_out, d_ff_20_q, or_3_out);
  and and_63 (and_63_out, not_46_out, not_65_out);
  D_Flip_Flop d_ff_25 (.D(DIVISION), .clk(DIVISION), .Q(d_ff_25_q), .reset(and_66_out));  // open: Qn, preset
  or or_29 (or_29_out, and_58_out, and_48_out, and_37_out, and_34_out);
  and and_64 (and_64_out, not_46_out, not_49_out);
  D_Flip_Flop d_ff_26 (.D(DIVISION), .clk(DIVISION), .Q(d_ff_26_q), .reset(and_68_out));  // open: Qn, preset
  LED led_9 (.in(or_29_out));
  xor xor_13 (xor_13_out, demultiplexer_5_out1, or_28_out);
  xor xor_14 (xor_14_out, demultiplexer_6_out1, or_28_out);
  xor xor_15 (xor_15_out, demultiplexer_7_out1, or_28_out);
  xor xor_16 (xor_16_out, demultiplexer_8_out1, or_28_out);
  D_Flip_Flop d_ff_27 (.D(or_3_out), .clk(not_36_out), .Q(d_ff_27_q), .reset(RESET));  // open: Qn, preset
  not not_36 (not_36_out, and_62_out);
  and and_65 (and_65_out, not_65_out, not_49_out);
  and and_66 (and_66_out, and_63_out, d_ff_25_q);
  and and_67 (and_67_out, not_49_out, not_54_out);
  and and_68 (and_68_out, and_64_out, d_ff_26_q);
  and and_69 (and_69_out, xnor_1_out, xnor_2_out, xnor_3_out, xnor_4_out);
  and and_70 (and_70_out, xor_13_out, or_28_out);
  and and_71 (and_71_out, xor_14_out, or_28_out);
  and and_72 (and_72_out, xor_15_out, or_28_out);
  and and_73 (and_73_out, xor_16_out, or_28_out);
  and and_74 (and_74_out, d_ff_30_q, and_76_out);
  not not_37 (not_37_out, d_ff_25_q);
  D_Flip_Flop d_ff_28 (.D(DIVISION), .clk(DIVISION), .Q(d_ff_28_q), .reset(and_65_out));  // open: Qn, preset
  not not_38 (not_38_out, d_ff_26_q);
  D_Flip_Flop d_ff_29 (.D(DIVISION), .clk(DIVISION), .Q(d_ff_29_q), .reset(and_67_out));  // open: Qn, preset
  and and_75 (and_75_out, not_39_out, not_40_out, not_41_out, not_42_out);
  not not_39 (not_39_out, d_ff_9_q);
  not not_40 (not_40_out, d_ff_8_q);
  not not_41 (not_41_out, d_ff_7_q);
  not not_42 (not_42_out, d_ff_6_q);
  Adder #(.width(1)) adder_5 (.a(and_70_out), .b(adder_6_cout), .out(adder_5_out));  // open: cin, cout
  Adder #(.width(1)) adder_6 (.a(and_71_out), .b(adder_7_cout), .out(adder_6_out), .cout(adder_6_cout));  // open: cin
  Adder #(.width(1)) adder_7 (.a(and_72_out), .b(adder_8_cout), .out(adder_7_out), .cout(adder_7_cout));  // open: cin
  Adder #(.width(1)) adder_8 (.a(and_73_out), .b(or_28_out), .out(adder_8_out), .cout(adder_8_cout));  // open: cin
  and and_76 (and_76_out, or_30_out, not_43_out);
  not not_43 (not_43_out, DIVISION);
  or or_30 (or_30_out, d_ff_27_q, d_ff_22_q);
  D_Flip_Flop d_ff_30 (.D(d_ff_22_q), .clk(and_2_out), .Q(d_ff_30_q), .reset(RESET));  // open: Qn, preset
  D_Flip_Flop d_ff_31 (.D(not_44_out), .clk(not_37_out), .Q(d_ff_31_q), .reset(RESET));  // open: Qn, preset
  not not_44 (not_44_out, d_ff_28_q);
  D_Flip_Flop d_ff_32 (.D(not_45_out), .clk(not_38_out), .Q(d_ff_32_q), .reset(RESET));  // open: Qn, preset
  not not_45 (not_45_out, d_ff_29_q);
  LED led_10 (.in(and_100_out));
  and and_77 (and_77_out, and_59_out, DIVISION);
  LED led_11 (.in(adder_5_out));
  LED led_12 (.in(adder_6_out));
  LED led_13 (.in(adder_7_out));
  LED led_14 (.in(adder_8_out));
  and and_78 (and_78_out, d_ff_19_qn, d_ff_18_qn);
  not not_46 (not_46_out, and_2_out);
  and and_79 (and_79_out, not_46_out, not_63_out);
  D_Flip_Flop d_ff_33 (.D(and_2_out), .clk(and_2_out), .Q(d_ff_33_q), .reset(RESET));  // open: Qn, preset
  D_Flip_Flop d_ff_34 (.D(and_77_out), .clk(and_77_out), .Q(d_ff_34_q), .reset(RESET));  // open: Qn, preset
  and and_80 (and_80_out, and_69_out, DIVISION);
  and and_81 (and_81_out, and_78_out, d_ff_16_qn);
  and and_82 (and_82_out, and_81_out, d_ff_17_qn);
  D_Flip_Flop d_ff_35 (.D(and_94_out), .clk(and_94_out), .Q(d_ff_35_q), .reset(RESET));  // open: Qn, preset
  D_Flip_Flop d_ff_36 (.D(d_ff_47_q), .clk(and_83_out), .Q(d_ff_36_q), .Qn(d_ff_36_qn), .reset(RESET));  // open: preset
  and and_83 (and_83_out, and_2_out, and_94_out);
  and and_84 (and_84_out, not_46_out, not_54_out);
  D_Flip_Flop d_ff_37 (.D(DIVISION), .clk(DIVISION), .Q(d_ff_37_q), .reset(and_85_out));  // open: Qn, preset
  and and_85 (and_85_out, and_84_out, d_ff_37_q);
  D_Flip_Flop d_ff_38 (.D(DIVISION), .clk(DIVISION), .Q(d_ff_38_q), .reset(and_86_out));  // open: Qn, preset
  and and_86 (and_86_out, and_79_out, d_ff_38_q);
  LED led_15 (.in(and_104_out));
  or or_31 (or_31_out, and_75_out, d_ff_34_q);
  and and_87 (and_87_out, and_80_out, not_48_out);
  not not_47 (not_47_out, and_82_out);
  not not_48 (not_48_out, d_ff_39_q);
  D_Flip_Flop d_ff_39 (.D(and_88_out), .clk(and_83_out), .Q(d_ff_39_q), .reset(RESET));  // open: Qn, preset
  and and_88 (and_88_out, and_94_out, d_ff_35_q);
  and and_89 (and_89_out, and_94_out, d_ff_36_q);
  not not_49 (not_49_out, d_ff_36_qn);
  and and_90 (and_90_out, not_54_out, not_62_out);
  and and_91 (and_91_out, not_63_out, not_65_out);
  not not_50 (not_50_out, d_ff_38_q);
  not not_51 (not_51_out, and_75_out);
  not not_52 (not_52_out, not_71_out);
  or or_32 (or_32_out, not_52_out, and_109_out, or_31_out);
  and and_92 (and_92_out, or_32_out, DIVISION);
  LED led_16 (.in(and_87_out));
  LED led_17 (.in(and_93_out));
  not not_53 (not_53_out, and_143_out);
  and and_93 (and_93_out, d_ff_39_q, not_57_out);
  and and_94 (and_94_out, not_47_out, DIVISION);
  D_Flip_Flop d_ff_40 (
    .D(and_89_out), .clk(and_83_out), .Q(d_ff_40_q), .Qn(d_ff_40_qn), .reset(RESET));  // open: preset
  not not_54 (not_54_out, d_ff_40_qn);
  not not_55 (not_55_out, d_ff_37_q);
  D_Flip_Flop d_ff_41 (.D(DIVISION), .clk(DIVISION), .Q(d_ff_41_q), .reset(and_90_out));  // open: Qn, preset
  D_Flip_Flop d_ff_42 (.D(DIVISION), .clk(DIVISION), .Q(d_ff_42_q), .reset(and_91_out));  // open: Qn, preset
  not not_56 (not_56_out, and_94_out);
  LED led_18 (.in(and_95_out));
  and and_95 (and_95_out, d_ff_43_q, not_58_out);
  not not_57 (not_57_out, d_ff_43_q);
  not not_58 (not_58_out, d_ff_47_q);
  D_Flip_Flop d_ff_43 (
    .D(and_96_out), .clk(and_83_out), .Q(d_ff_43_q), .Qn(d_ff_43_qn), .reset(RESET));  // open: preset
  and and_96 (and_96_out, and_94_out, d_ff_39_q);
  D_Flip_Flop d_ff_44 (
    .D(and_97_out), .clk(and_83_out), .Q(d_ff_44_q), .Qn(d_ff_44_qn), .reset(RESET));  // open: preset
  and and_97 (and_97_out, and_94_out, d_ff_40_q);
  D_Flip_Flop d_ff_45 (.D(not_59_out), .clk(not_55_out), .Q(d_ff_45_q), .reset(RESET));  // open: Qn, preset
  not not_59 (not_59_out, d_ff_41_q);
  D_Flip_Flop d_ff_46 (.D(not_60_out), .clk(not_50_out), .Q(d_ff_46_q), .reset(RESET));  // open: Qn, preset
  not not_60 (not_60_out, d_ff_42_q);
  and and_98 (and_98_out, not_56_out, not_71_out, DIVISION);
  and and_99 (and_99_out, and_98_out, d_ff_33_q, not_51_out);
  and and_100 (and_100_out, and_92_out, not_70_out);
  LED led_19 (.in(demultiplexer_9_out0));
  LED led_20 (.in(demultiplexer_9_out1));
  LED led_21 (.in(demultiplexer_10_out0));
  Demultiplexer demultiplexer_9 (
    .out0(demultiplexer_9_out0), .out1(demultiplexer_9_out1), .in(and_101_out), .sel(and_111_out));
  and and_101 (and_101_out, d_ff_47_q, d_ff_36_qn);
  not not_61 (not_61_out, d_ff_36_qn);
  and and_102 (and_102_out, and_94_out, d_ff_43_q);
  and and_103 (and_103_out, and_94_out, d_ff_44_q);
  not not_62 (not_62_out, d_ff_44_qn);
  not not_63 (not_63_out, d_ff_43_qn);
  LED led_22 (.in(d_ff_49_q));
  and and_104 (and_104_out, not_53_out, and_99_out);
  and and_105 (and_105_out, and_1_out, d_ff_20_q, not_69_out);
  LED led_23 (.in(demultiplexer_10_out1));
  LED led_24 (.in(demultiplexer_11_out0));
  LED led_25 (.in(demultiplexer_11_out1));
  Demultiplexer demultiplexer_10 (
    .out0(demultiplexer_10_out0), .out1(demultiplexer_10_out1), .in(and_106_out), .sel(and_111_out));
  Demultiplexer demultiplexer_11 (
    .out0(demultiplexer_11_out0), .out1(demultiplexer_11_out1), .in(and_107_out), .sel(and_111_out));
  and and_106 (and_106_out, not_61_out, d_ff_40_qn);
  and and_107 (and_107_out, not_64_out, d_ff_44_qn);
  not not_64 (not_64_out, d_ff_40_qn);
  D_Flip_Flop d_ff_47 (
    .D(and_102_out), .clk(and_83_out), .Q(d_ff_47_q), .Qn(d_ff_47_qn), .reset(RESET));  // open: preset
  D_Flip_Flop d_ff_48 (
    .D(and_103_out), .clk(and_83_out), .Q(d_ff_48_q), .Qn(d_ff_48_qn), .reset(RESET));  // open: preset
  not not_65 (not_65_out, d_ff_47_qn);
  LED led_26 (.in(d_ff_45_q));
  LED led_27 (.in(d_ff_46_q));
  LED led_28 (.in(d_ff_32_q));
  LED led_29 (.in(d_ff_31_q));
  D_Flip_Flop d_ff_49 (.D(or_33_out), .clk(or_33_out), .Q(d_ff_49_q), .reset(RESET));  // open: Qn, preset
  or or_33 (or_33_out, and_105_out, d_ff_53_q, and_112_out);
  LED led_30 (.in(demultiplexer_12_out0));
  LED led_31 (.in(demultiplexer_12_out1));
  LED led_32 (.in(demultiplexer_13_out0));
  Demultiplexer demultiplexer_12 (
    .out0(demultiplexer_12_out0), .out1(demultiplexer_12_out1), .in(and_108_out), .sel(and_111_out));
  and and_108 (and_108_out, not_66_out, d_ff_48_qn);
  not not_66 (not_66_out, d_ff_44_qn);
  not not_67 (not_67_out, d_ff_48_qn);
  and and_109 (and_109_out, not_68_out, d_ff_48_q);
  not not_68 (not_68_out, and_104_out);
  LED led_33 (.in(demultiplexer_13_out1));
  Demultiplexer demultiplexer_13 (
    .out0(demultiplexer_13_out0), .out1(demultiplexer_13_out1), .in(and_110_out), .sel(and_111_out));
  and and_110 (and_110_out, not_67_out, not_67_out);
  and and_111 (and_111_out, or_34_out, not_70_out);
  or or_34 (or_34_out, d_ff_45_q, d_ff_46_q, d_ff_32_q, d_ff_31_q);
  not not_69 (not_69_out, or_3_out);
  not not_70 (not_70_out, d_ff_11_q);
  LED led_34 (.in(d_ff_1_q));
  LED led_35 (.in(OVERRIDE));
  and and_112 (and_112_out, and_1_out, and_123_out);
  and and_113 (and_113_out, adder_5_out, adder_6_out, adder_7_out, adder_8_out);
  and and_114 (and_114_out, adder_5_out, adder_6_out, adder_7_out);
  and and_115 (and_115_out, adder_5_out, adder_6_out, adder_8_out);
  and and_116 (and_116_out, adder_5_out, adder_6_out);
  and and_117 (and_117_out, adder_5_out, adder_8_out, adder_7_out);
  and and_118 (and_118_out, adder_5_out, adder_7_out);
  and and_119 (and_119_out, adder_5_out, adder_8_out);
  and and_120 (and_120_out, adder_7_out, adder_6_out, adder_8_out);
  and and_121 (and_121_out, adder_7_out, adder_6_out);
  and and_122 (and_122_out, adder_6_out, adder_8_out);
  LED led_36 (.in(d_ff_1_q));
  not not_71 (not_71_out, d_ff_51_q);
  D_Flip_Flop d_ff_50 (.D(and_2_out), .clk(and_2_out), .Q(d_ff_50_q), .reset(RESET));  // open: Qn, preset
  not not_72 (not_72_out, and_141_out);
  and and_123 (and_123_out, or_3_out, or_35_out);
  or or_35 (or_35_out, and_124_out, and_125_out, and_126_out, and_127_out, and_128_out, and_129_out, and_130_out, and_131_out, and_132_out, and_133_out, and_134_out, and_135_out, and_137_out, and_138_out, and_139_out, and_140_out);
  and and_124 (and_124_out, and_113_out, or_7_out);
  and and_125 (and_125_out, and_114_out, or_8_out);
  and and_126 (and_126_out, and_115_out, or_9_out);
  and and_127 (and_127_out, and_116_out, or_10_out);
  and and_128 (and_128_out, and_117_out, or_16_out);
  and and_129 (and_129_out, and_118_out, or_15_out);
  and and_130 (and_130_out, and_119_out, or_18_out);
  and and_131 (and_131_out, adder_5_out, d_ff_9_q);
  and and_132 (and_132_out, and_120_out, or_17_out);
  and and_133 (and_133_out, and_121_out, or_19_out);
  and and_134 (and_134_out, and_122_out, and_11_out);
  and and_135 (and_135_out, adder_6_out, and_11_out);
  and and_136 (and_136_out, adder_8_out, adder_7_out);
  and and_137 (and_137_out, and_136_out, or_22_out);
  and and_138 (and_138_out, adder_7_out, and_22_out);
  and and_139 (and_139_out, adder_8_out, and_14_out);
  LED led_37 (.in(and_141_out));
  LED led_38 (.in(not_73_out));
  not not_73 (not_73_out, d_ff_1_q);
  D_Flip_Flop d_ff_51 (.D(d_ff_22_q), .clk(d_ff_50_q), .Q(d_ff_51_q), .reset(RESET));  // open: Qn, preset
  LED led_39 (.in(and_142_out));
  D_Flip_Flop d_ff_52 (.D(d_ff_48_q), .clk(and_83_out), .Q(d_ff_52_q), .reset(RESET));  // open: Qn, preset
  and and_140 (and_140_out, and_14_out, and_16_out);
  and and_141 (and_141_out, d_ff_51_q, DIVISION);
  D_Flip_Flop d_ff_53 (.D(d_ff_52_q), .clk(and_83_out), .Q(d_ff_53_q), .reset(RESET));  // open: Qn, preset
  LED led_40 (.in(and_143_out));
  not not_74 (not_74_out, d_ff_53_q);
  and and_142 (and_142_out, d_ff_49_q, not_72_out, not_74_out);
  and and_143 (and_143_out, d_ff_53_q, not_72_out, d_ff_49_q);

  // Notes on the sheet:
  //   MODE
  //   0=ADDITION
  //   1=SUBTRACTION
  //    OUTPUT 
  //   SYSTEM HALT
  //   B
  //   A
  //   1
  //   2
  //   4
  //   DATA BITS
  //   SELECTOR=0
  //   8
  //   SELECTOR=1
  //   COMPARATOR
  //   UNIT
  //   REPEATED ADDITON FEEDBACK LOGIC
  //   SIGNED RANGE OVERFLOW DETECTION UNIT
  //   BIT LOCK
  //   DETECTOR
  //   MUTIPLICAND
  //   ABSENT
  //   2's COMLEMENT 
  //   ENABLER
  //   MULTIPLIER ABSENCE 
  //   OUTPUT
  //   FEEDBACK
  //   SYSTEM
  //   AUTOMATED
  //   SUBTRACTION
  //   OUTPUT FORM 
  //   CORRECTION
  //   MULTIPLIER 
  //   ABSENT
  //   8
  //   4
  //   2
  //   1
  //   16
  //   MULTIPLICATIVE CONVERGENCE
  //   ACHEIVED
  //   REPEATED ARITHMETIC MACHINE
  //   CONVERGENCE ERROR
  //   -8
  //   -4
  //   -2
  //   -1
  //   DIVISIBILITY CONVERGENCE 
  //   ACHEIVED
  //   1
  //   2
  //   ACTIVATION
  //   3
  //   SERIES FLIP FLOP SIMULTANEOUS
  //   DETECTORS
  //   REPEATED SUBTRACTION FEEDBACK LOGIC
  //   4
  //   3
  //   5
  //   OVERFLOW ERROR INDUCED 
  //   IN SYSTEM
  //   4
  //   6
  //   5
  //   7
  //   6
  //   8
  //   FLIP FLOP 
  //   OVERSHOOT  
  //   CORRECTION
  //   LOGIC
  //   7
  //   SYSTEM HALTED
  //   TO PREVENT 
  //   DATA CORRRUPTION
  //   SYSTEM HALT
  //   OVERRIDEN
  //   CLOCK 
  //   DISENGAGED
  //   INPUT FORM 
  //   INVALID
  //   CLOCK 
  //   ENGAGED
  //   INVALID SYNTAX DETECTOR
  //   FEEDBACK 
  //   OVERFLOW
  //   OVERFLOW TYPE
  //   OUTPUT 
  //   OVERFLOW
endmodule
